# Fritzing sketch leds (saved by Fritzing 0.9.3b)
breadboards: 1

parts:
  BAT1 = Battery Holders [package=battcom_20mm_pth]
  LED2 = LED - 3mm [color="Red (633nm)" package="3 mm [THT]"]
  R1 = Resistor [tolerance=±5% resistance=220 package="2010 [SMD]"]
  R3 = Resistor [tolerance=±5% resistance=220 package="2010 [SMD]"]

nets:
  N1: BAT1.+, LED2.anode
  N2: LED2.cathode, R1.Pin_0, R3.Pin_0, R3.Pin_1
