# Fritzing sketch programming (saved by Fritzing 0.9.3b)
breadboards: 1

parts:
  BAT1 = Battery Holders [package=battcom_20mm_pth]
  U1 = ATTINY13 [package=dip]
  LED1 = LED - 3mm [color="Red (633nm)" package="3 mm [THT]"]
  LED2 = LED - 3mm [color="Red (633nm)" package="3 mm [THT]"]
  R1 = Resistor [tolerance=±5% resistance=220 package="2010 [SMD]"]
  R2 = Resistor [tolerance=±5% resistance=220 package="2010 [SMD]"]

nets:
  N1: BAT1.+, U1.VCC
  N2: U1.GND, R1.Pin_1, R2.Pin_1
  N3: U1.PB0(MOSI), LED2.anode
  N4: U1.PB1(MISO), LED1.anode
  N5: LED1.cathode, R1.Pin_0
  N6: LED2.cathode, R2.Pin_0
